# Fritzing sketch B.ob_Wiring (saved by Fritzing 0.9.6b)
perfboards: 1

parts:
  ACT_BLDC-8015A-5_Right = IC, SIP package, 20 pins [chip_label=IC]
  ACT_BLDC-8015A-5_Left = IC, SIP package, 20 pins [chip_label=IC]
  Battery_20V = Power plug
  Buck-Converter = RioRand LM2596
  Raspberry_Pi_4B = Raspberry Pi 4B
  USB-C = USB Connectors [part_number=U1 package=usb-mb-h]
  Right_Motor = SIP - 8 pins [package="SIP (Single Inline) [THT]"]
  Left_Motor = SIP - 8 pins [package="SIP (Single Inline) [THT]"]
  R2 = Resistor [tolerance=±5% power=0.25 resistance=220 package=THT]
  R3 = Resistor [tolerance=±5% power=0.25W resistance=1k package=THT]
  R1 = Resistor [tolerance=±5% power=0.25 resistance=220 package=THT]
  R4 = Resistor [tolerance=±5% power=0.25 resistance=1k package=THT]
  Q1 = MOSFET-NCHANNEL [package=sot23-3]
  R5 = Resistor [tolerance=±5% power=0.25 resistance=10k package=THT]
  R6 = Resistor [tolerance=±5% power=0.25 resistance=10k package=THT]
  Q2 = MOSFET-NCHANNEL [package=sot23-3]
  R7 = Resistor [tolerance=±5% power=0.25 resistance=10k package=THT]
  R8 = Resistor [tolerance=±5% power=0.25 resistance=10k package=THT]
  S1 = Round Pushbutton [part_number="Emergency Button"]
  LI1 = RPlidar A1M8 [package=THT]
  U2 = Hirose DF13 Series Header [part_number="USB Adapter" package=DF13C-8P-1.25V]
  USBTTL2 = Micro USB B Plug
  USBTTL1 = USB A Plug

nets:
  GND: ACT_BLDC-8015A-5_Right.pin2, ACT_BLDC-8015A-5_Left.pin2, Raspberry_Pi_4B.GND, S1.leg1
  RIGHT_ALM: ACT_BLDC-8015A-5_Right.pin3, Raspberry_Pi_4B.GPIO25, R2.Pin_1
  RIGHT_ENCODER: ACT_BLDC-8015A-5_Right.pin4, Raspberry_Pi_4B.GPIO24, R4.Pin_1
  RIGHT_PWM: ACT_BLDC-8015A-5_Right.pin5, Raspberry_Pi_4B.GPIO12
  LEFT_ENBL/RIGHT_ENBL: ACT_BLDC-8015A-5_Right.pin7, ACT_BLDC-8015A-5_Left.pin7, S1.leg0
  M_RIGHT_F/R: ACT_BLDC-8015A-5_Right.pin8, Q2.D, R8.Pin_1
  N1: ACT_BLDC-8015A-5_Right.pin9, Right_Motor.REF-
  N2: ACT_BLDC-8015A-5_Right.pin10, Right_Motor.HW
  N3: ACT_BLDC-8015A-5_Right.pin11, Right_Motor.HV
  N4: ACT_BLDC-8015A-5_Right.pin12, Right_Motor.HU
  N5: ACT_BLDC-8015A-5_Right.pin13, Right_Motor.REF+
  N6: ACT_BLDC-8015A-5_Right.pin16, ACT_BLDC-8015A-5_Left.pin16, Battery_20V.GND, Buck-Converter.Pin_2
  N7: ACT_BLDC-8015A-5_Right.pin17, ACT_BLDC-8015A-5_Left.pin17, Battery_20V.VCC, Buck-Converter.Pin_1
  N8: ACT_BLDC-8015A-5_Right.pin18, Right_Motor.U
  N9: ACT_BLDC-8015A-5_Right.pin19, Right_Motor.V
  N10: ACT_BLDC-8015A-5_Right.pin20, Right_Motor.W
  LEFT_ALM: ACT_BLDC-8015A-5_Left.pin3, Raspberry_Pi_4B.GPIO22, R1.Pin_1
  LEFT_ENCODER: ACT_BLDC-8015A-5_Left.pin4, Raspberry_Pi_4B.GPIO23, R3.Pin_1
  LEFT_PWM: ACT_BLDC-8015A-5_Left.pin5, Raspberry_Pi_4B.GPIO13
  M_LEFT_F/R: ACT_BLDC-8015A-5_Left.pin8, Q1.D, R7.Pin_1
  N11: ACT_BLDC-8015A-5_Left.pin9, Left_Motor.REF-
  N12: ACT_BLDC-8015A-5_Left.pin10, Left_Motor.HW
  N13: ACT_BLDC-8015A-5_Left.pin11, Left_Motor.HV
  N14: ACT_BLDC-8015A-5_Left.pin12, Left_Motor.HU
  N15: ACT_BLDC-8015A-5_Left.pin13, Left_Motor.REF+
  N16: ACT_BLDC-8015A-5_Left.pin18, Left_Motor.U
  N17: ACT_BLDC-8015A-5_Left.pin19, Left_Motor.V
  N18: ACT_BLDC-8015A-5_Left.pin20, Left_Motor.W
  N19: Buck-Converter.Pin_3, USB-C.D+
  N20: Buck-Converter.Pin_4, USB-C.D-
  3.3V: Raspberry_Pi_4B.3V3, R2.Pin_0, R3.Pin_0, R1.Pin_0, R4.Pin_0, Q1.G, R5.Pin_0, R6.Pin_0, Q2.G
  5V: Raspberry_Pi_4B.5V, R7.Pin_0, R8.Pin_0
  LEFT_F/R: Raspberry_Pi_4B.GPIO6, Q1.S, R5.Pin_1
  RIGHT_F/R: Raspberry_Pi_4B.GPIO19, R6.Pin_1, Q2.S
  Power_In: USB-C.GND, USB-C.VBUS
  N21: LI1.pin1, U2.Tx
  N22: LI1.pin2, U2.Rx
  N23: LI1.pin3, U2.5V
  N24: LI1.pin4, U2.GND
  N25: LI1.pin5, U2.GND_MOTO
  N26: LI1.pin6, U2.CTRL_MOTO
  N27: LI1.pin7, U2.5V_MOTO
  OUTPUT_USB: U2.OUTPUT
  N28: USBTTL2.usb, USBTTL1.usb

notes:
  20V -> 5V
  Right_Motor
  Left_Motor
  default: closed
  IC1
  IC2
  D
  S
  G
  LIDAR

custom parts:
  SIP - 8 pins: A SIP stand-in part for whatever you want. With 8 pins on a 300 mil single inline package (SIP) footprint.
  RPlidar A1M8: .The RPLIDAR A1 is the next generation low cost 360 degree 2D laser scanner (LIDAR) solution developed by SLAMTEC. It can take up to 4000 samples of laser ranging per second with high rotation speed. And equipped with SLAMTEC patented OPTMAG technology, it breakouts the life limitation of traditional LIDAR system so as to work stably for a long time.
  Hirose DF13 Series Header: Hirose DF13 Header: 1.25mm Pitch Miniature Crimping Connector. Single Row Straight Pin Header (SMT)
